# Fritzing sketch ESP32_DevKiteC_A4988 (saved by Fritzing 0.9.3b)
breadboards: 9

parts:
  Pololu_A1 = Pololu A4988 [package=SO16]
  MH-ET_LIVE_ESP32_DEVKIT1 = MH-ET LIVE ESP32 DEVKIT 38 pins
  Power_plug1 = Power plug [part_number=12V]
  Pololu_A3 = Pololu A4988 [package=SO16]
  Pololu_A4 = Pololu A4988 [package=SO16]
  LED1 = LED - 5mm [color="Red (633nm)" package="5 mm [THT]"]
  M2 = Stepper Motor - Bipolar
  M3 = Stepper Motor - Bipolar
  M4 = DC Motor [part_number=fan]
  R1 = Temperature Sensor (Thermistor) [thermistor_type=NTC package=THT]  # not connected
  GLCD_128x1 = 128 x 64 Graphic LCD [part_number="Taojingchi LCD"]
  M1 = Stepper Motor - Bipolar
  IC1 = DIP - 6 pins [chip_label="5V RELAY" package="DIP (Dual Inline) [THT]"]
  IC2 = DIP - 6 pins [chip_label="5V RELAY" package="DIP (Dual Inline) [THT]"]
  R2 = Resistor [tolerance=±5% resistance=220 package=THT]
  R3 = Temperature Sensor (Thermistor) [thermistor_type=NTC package=THT]
  R4 = Resistor [tolerance=±5% resistance=100 package=THT]

nets:
  N1: Pololu_A1.RESET, Pololu_A1.SLEEP
  N2: Pololu_A1.STEP, MH-ET_LIVE_ESP32_DEVKIT1.IO27
  N3: Pololu_A1.DIR, MH-ET_LIVE_ESP32_DEVKIT1.IO26
  N4: Pololu_A1.GND#8, MH-ET_LIVE_ESP32_DEVKIT1.GND#64, Pololu_A3.GND#8, Pololu_A4.GND#8, GLCD_128x1.1_Vss, IC1.DC-, IC2.DC-, R3.pin_0
  VDD: Pololu_A1.VDD, MH-ET_LIVE_ESP32_DEVKIT1.5V, Pololu_A3.VDD, Pololu_A4.VDD, GLCD_128x1.2_Vdd, IC1.DC+, IC2.DC+, R4.Pin_1
  N5: Pololu_A1.1B, M1.B
  N6: Pololu_A1.1A, M1.A
  N7: Pololu_A1.2A, M1.C
  N8: Pololu_A1.2B, M1.D
  N9: Pololu_A1.GND#14, Power_plug1.GND, Pololu_A3.GND#14, Pololu_A4.GND#14, M4.pin_1, R2.Pin_0
  N10: Pololu_A1.VMOT, Power_plug1.VCC, Pololu_A3.VMOT, Pololu_A4.VMOT, IC1.CO, IC2.CO
  N11: MH-ET_LIVE_ESP32_DEVKIT1.IO32, R3.pin_1, R4.Pin_0
  N12: MH-ET_LIVE_ESP32_DEVKIT1.IO33, Pololu_A4.DIR
  N13: MH-ET_LIVE_ESP32_DEVKIT1.IO25, Pololu_A4.STEP
  N14: MH-ET_LIVE_ESP32_DEVKIT1.IO14, Pololu_A3.DIR
  N15: MH-ET_LIVE_ESP32_DEVKIT1.IO12, Pololu_A3.STEP
  N16: MH-ET_LIVE_ESP32_DEVKIT1.IO19, IC2.IN
  N17: MH-ET_LIVE_ESP32_DEVKIT1.IO18, IC1.IN
  N18: Pololu_A3.RESET, Pololu_A3.SLEEP
  N19: Pololu_A3.1B, M3.B
  N20: Pololu_A3.1A, M3.A
  N21: Pololu_A3.2A, M3.C
  N22: Pololu_A3.2B, M3.D
  N23: Pololu_A4.RESET, Pololu_A4.SLEEP
  N24: Pololu_A4.1B, M2.B
  N25: Pololu_A4.1A, M2.A
  N26: Pololu_A4.2A, M2.C
  N27: Pololu_A4.2B, M2.D
  N28: LED1.cathode, R2.Pin_1
  N29: LED1.anode, IC2.NO
  N30: M4.pin_2, IC1.NO

custom parts:
  MH-ET LIVE ESP32 DEVKIT 38 pins: http://mh.nodebb.com/topic/2/mh-et-live-esp32-devkit
  DIP - 6 pins: A DIP stand-in part for whatever IC you want. With 6 pins on a 300mil dual inline package (DIP) footprint.
